# Fritzing sketch projet en fritzing (saved by Fritzing 0.9.3b)
breadboards: 1

parts:
  Composant1 = Arduino Uno (Rev3)
  R4 = Resistor [tolerance=±5% resistance=270 package="1206 [SMD]"]
  LED1 = RGB LED (com. anode, rbg) [package="5 mm [THT]"]
  R5 = Resistor [tolerance=±5% resistance=270 package="1206 [SMD]"]
  R6 = Resistor [tolerance=±5% resistance=270 package="1206 [SMD]"]
  R7 = Resistor [tolerance=±5% resistance=270 package="1206 [SMD]"]
  C1 = Ceramic Capacitor [capacitance=0.1mF package="0805 [SMD, multilayer]"]
  R8 = Resistor [tolerance=±5% resistance=1M package="1206 [SMD]"]
  D1 = Rectifier Diode [part_number=1N4001 package="Melf DO-213 AB [SMD]"]
  C2 = Ceramic Capacitor [capacitance=50nF voltage=5V package="0805 [SMD, multilayer]"]
  L1 = Inductor [inductance=10mH package="1206 [SMD]"]
  R9 = Resistor [tolerance=±5% resistance=3.3k package="1206 [SMD]"]
  R10 = Resistor [tolerance=±5% resistance=10 package="1206 [SMD]"]

nets:
  N1: Composant1.A0, C1.0, R8.Pin_0, D1.anode
  N2: Composant1.D9_PWM, R10.Pin_0
  N3: Composant1.D10_PWM/SS, R7.Pin_0
  N4: Composant1.D11_PWM/MOSI, R6.Pin_0
  N5: Composant1.D12/MISO, R4.Pin_0
  N6: Composant1.GND, C1.1, R8.Pin_1, R9.Pin_0
  N7: Composant1.5V, R5.Pin_0
  N8: R4.Pin_1, LED1.red_cathode
  N9: LED1.common_anode, R5.Pin_1
  N10: LED1.blue_cathode, R6.Pin_1
  N11: LED1.green_cathode, R7.Pin_1
  N12: D1.cathode, C2.0, R10.Pin_1
  N13: C2.1, L1.pin_1, R9.Pin_1
